// Logisim project coconut16.circ as structural Verilog: 1 circuit, main circuit main
module main (
  input  [19:0] in_1
);

  wire clk, comparator_1_eq, comparator_1_gt, comparator_1_lt, comparator_2_eq, comparator_2_gt, io_sel,
       not_1_out, or_2_out, ram_sel, rd_wr_prime, rom_sel;
  wire [11:0] io_address;
  wire [15:0] controlled_buffer_1_out, data, fp, r0, r1, r2, r3, r4, r5, r6, undriven;
  wire [19:0] physical_address;

  Clock clock_1 (.out(clk));
  // Probe on fp
  // Probe on r6
  // Probe on r5
  // Probe on r4
  // Probe on r3
  // Probe on r2
  // Probe on r1
  // Probe on r0
  assign controlled_buffer_1_out = rd_wr_prime ? data : 16'bz;  // Controlled_Buffer controlled_buffer_1
  assign data = not_1_out ? undriven : 16'bz;  // Controlled_Buffer controlled_buffer_2
  not not_1 (not_1_out, rd_wr_prime);
  // Probe on physical_address
  Bit_Extender #(.in_width(20), .out_width(12)) bit_extender_1 (.in(physical_address), .out(io_address));
  Comparator #(.width(20), .mode("unsigned")) comparator_1 (
    .a(physical_address), .b(20'hff000), .gt(comparator_1_gt), .eq(comparator_1_eq), .lt(comparator_1_lt));
  Comparator #(.width(20), .mode("unsigned")) comparator_2 (
    .a(physical_address), .b(20'hfe000), .gt(comparator_2_gt), .eq(comparator_2_eq), .lt(ram_sel));
  or or_1 (io_sel, comparator_1_gt, comparator_1_eq);
  and and_1 (rom_sel, comparator_1_lt, or_2_out);
  or or_2 (or_2_out, comparator_2_gt, comparator_2_eq);

  // Other names for the same wires on the sheet: rom_address[11:0] = io_address
endmodule
